# Fritzing sketch distanceSensor (saved by Fritzing 0.9.2b)
breadboards: 1

parts:
  Part1 = SRF05 Ultrasonic Rangefinder
  R1 = Resistor [tolerance=±5% resistance=2.2k package="2512 [SMD]"]
  R2 = Resistor [tolerance=±5% resistance=1k package="0402 [SMD]"]
  Raspberry_Pi1 = Raspberry Pi 2

nets:
  VCC: Part1.VCC, Raspberry_Pi1.5V
  N1: Part1.Trig, Raspberry_Pi1.GPIO23
  N2: Part1.Echo, R2.Pin_0
  GND: Part1.GND, R1.Pin_1, Raspberry_Pi1.GND
  N3: R1.Pin_0, R2.Pin_1, Raspberry_Pi1.GPIO24
