# Fritzing sketch xmasTree (saved by Fritzing 0.9.2b)
breadboards: 1

parts:
  LED1 = LED - 5mm [color="Red (633nm)" package="5 mm [THT]"]
  LED2 = LED - 5mm [color="Red (633nm)" package="5 mm [THT]"]
  LED3 = LED - 5mm [color="Red (633nm)" package="5 mm [THT]"]
  LED4 = LED - 5mm [color="Red (633nm)" package="5 mm [THT]"]
  LED5 = LED - 5mm [color="Red (633nm)" package="5 mm [THT]"]
  R1 = Resistor [tolerance=±5% resistance=220 package=THT]
  R2 = Resistor [tolerance=±5% resistance=220 package=THT]
  LED6 = LED - 5mm [color="Red (633nm)" package="5 mm [THT]"]
  LED7 = LED - 5mm [color="Red (633nm)" package="5 mm [THT]"]
  LED8 = LED - 5mm [color="Red (633nm)" package="5 mm [THT]"]
  LED9 = LED - 5mm [color="Red (633nm)" package="5 mm [THT]"]
  LED10 = LED - 5mm [color="Red (633nm)" package="5 mm [THT]"]
  Raspberry_Pi2 = Raspberry Pi 2
  LED11 = RGB LED (com. anode, rbg) [package="5 mm [THT]"]
  R4 = Resistor [tolerance=±5% resistance=220 package="0805 [SMD]"]
  R5 = Resistor [tolerance=±5% resistance=220 package="0805 [SMD]"]
  R6 = Resistor [tolerance=±5% resistance=220 package="0805 [SMD]"]

nets:
  N1: LED1.cathode, LED2.cathode, LED3.cathode, LED4.cathode, LED5.cathode, LED6.cathode, LED7.cathode, LED8.cathode, LED9.cathode, LED10.cathode, Raspberry_Pi2.GND, LED11.common_anode
  N2: LED1.anode, LED2.anode, LED3.anode, LED4.anode, LED5.anode, R1.Pin_1
  N3: R1.Pin_0, Raspberry_Pi2.GPIO17
  N4: R2.Pin_0, Raspberry_Pi2.GPIO4
  N5: R2.Pin_1, LED6.anode, LED7.anode, LED8.anode, LED9.anode, LED10.anode
  N6: Raspberry_Pi2.GPIO5, R6.Pin_1
  N7: Raspberry_Pi2.GPIO6, R4.Pin_1
  N8: Raspberry_Pi2.GPIO13, R5.Pin_1
  N9: LED11.red_cathode, R6.Pin_0
  N10: LED11.blue_cathode, R4.Pin_0
  N11: LED11.green_cathode, R5.Pin_0
